# Fritzing sketch layout (saved by Fritzing 1.0.6)

parts:
  Part1 = Arduino Uno (Rev3) - ICSP
  S1 = H-Bridge with L298N
  Part2 = Bluetooth HC-05 Macho
  M1 = DC Motor [voltage_(max)=6V voltage_(min)=3V]
  M2 = DC Motor [voltage_(max)=6V voltage_(min)=3V]
  M3 = DC Motor [voltage_(max)=6V voltage_(min)=3V]
  M4 = DC Motor [voltage_(max)=6V voltage_(min)=3V]
  VCC1 = Battery

nets:
  GND: Part1.GND, S1.GND, Part2.GND
  N1: Part1.D0/RX, Part2.TXD
  N2: Part1.D1/TX, Part2.RXD
  3V3: Part1.3V3, Part2.VCC
  N3: S1.12V, VCC1.+
  N4: S1.M1-01, M3.pin_1, M4.pin_1
  N5: S1.M1-02, M3.pin_2, M4.pin_2
  N6: S1.M2-01, M1.pin_1, M2.pin_1
  N7: S1.M2-02, M1.pin_2, M2.pin_2

custom parts:
  H-Bridge with L298N: h-bridge
  Battery: Your standard 2x 18650 battery pack (7,4 Volts)
